# Fritzing sketch color_picker (saved by Fritzing 0.9.3b)
breadboards: 1

parts:
  RE1 = Rotary Encoder [package=THT]
  R1 = Resistor [tolerance=±5% resistance=330 package=THT]
  R2 = Resistor [tolerance=±5% resistance=330 package=THT]
  R3 = Resistor [tolerance=±5% resistance=330 package=THT]
  LED1 = RGB LED - (4 legs) [package="5 mm [THT]"]
  S1 = Pushbutton [package="[THT]"]
  Raspberry_Pi_1 = Raspberry Pi 2

nets:
  N1: RE1.EncoderPinA, Raspberry_Pi_1.GIPO16
  N2: RE1.EncoderPinC, Raspberry_Pi_1.GND
  N3: RE1.EncoderPinB, Raspberry_Pi_1.GIPO20
  N4: R1.Pin_0, Raspberry_Pi_1.GIPO22
  N5: R1.Pin_1, LED1.red_cathode
  N6: R2.Pin_0, Raspberry_Pi_1.GIPO23
  N7: R2.Pin_1, LED1.green_cathode
  N8: R3.Pin_0, Raspberry_Pi_1.GIPO24
  N9: R3.Pin_1, LED1.blue_cathode
  3V3: LED1.common_anode, S1.Pin_1, S1.Pin_2, Raspberry_Pi_1.3v3, Raspberry_Pi_1.3V3
  N10: S1.Pin_3, S1.Pin_4, Raspberry_Pi_1.GIPO21
