# Fritzing sketch rgb_led (saved by Fritzing 0.9.2b)
breadboards: 1

parts:
  Raspberry_Pi1 = Raspberry Pi 2
  LED1 = RGB LED (com. cathode, rgb) [package="5 mm [THT]"]
  R1 = Resistor [tolerance=±5% resistance=330 package=THT]

nets:
  N1: Raspberry_Pi1.GPIO10, LED1.green_anode
  N2: Raspberry_Pi1.GPIO9, LED1.red_anode
  N3: Raspberry_Pi1.GPIO11, LED1.blue_anode
  N4: Raspberry_Pi1.GND, R1.Pin_0
  N5: LED1.common_cathode, R1.Pin_1
